# Fritzing sketch SchemaFritzing (saved by Fritzing 0.9.3b)
breadboards: 2

parts:
  Raspberry_Pi_1 = Raspberry Pi 3 [part_number=RPI-3-V1.2]
  Componente1 = Arduino Uno (Rev3)
  J1 = Basic Servo
  LED1 = LED - 5mm [color="Green (555nm)" package="5 mm [THT]"]
  R1 = Resistor [tolerance=±5% resistance=220 package=THT]
  U3 = HC-SR04 [chip_label=IC package="SIP (Single Inline) [THT]"]
  R2 = Resistor [tolerance=±5% resistance=220 package=THT]
  R3 = Resistor [tolerance=±5% resistance=220 package=THT]
  R4 = Resistor [tolerance=±5% resistance=220 package=THT]
  LED2 = LED - 5mm [color="Red (633nm)" package="5 mm [THT]"]
  LED3 = LED - 5mm [color="Green (555nm)" package="5 mm [THT]"]
  LED4 = LED - 5mm [color="Green (555nm)" package="5 mm [THT]"]
  S1 = Pushbutton [package="[THT]"]
  S2 = Pushbutton [package="[THT]"]
  R6 = Resistor [tolerance=±5% resistance=10k package=THT]
  R7 = Resistor [tolerance=±5% resistance=10k package=THT]
  R8 = Rotary Potentiometer (Small) [maximum_resistance=100kΩ package=THT]

nets:
  N1: Raspberry_Pi_1.3v3, S1.Pin_1, S1.Pin_2, S2.Pin_1, S2.Pin_2
  N2: Raspberry_Pi_1.GIPO17, R4.Pin_1
  N3: Raspberry_Pi_1.GIPO27, R3.Pin_1
  N4: Raspberry_Pi_1.GIPO22, R2.Pin_1
  N5: Raspberry_Pi_1.GIPO24, S1.Pin_3, S1.Pin_4, R6.Pin_0
  N6: Raspberry_Pi_1.GIPO23, S2.Pin_3, S2.Pin_4, R7.Pin_0
  N7: Raspberry_Pi_1.GND, LED2.cathode, LED3.cathode, LED4.cathode, R6.Pin_1, R7.Pin_1
  N8: Componente1.A0, R8.wiper
  N9: Componente1.D10_PWM/SS, J1.pulse
  N10: Componente1.D4, R1.Pin_1
  N11: Componente1.D6_PWM, U3.Echo
  N12: Componente1.D7, U3.Trig
  VCC: Componente1.5V, J1.vcc, U3.Vcc, R8.leg2
  GND: Componente1.GND, J1.gnd, LED1.cathode, U3.GND, R8.leg1
  N13: LED1.anode, R1.Pin_0
  N14: R2.Pin_0, LED2.anode
  N15: R3.Pin_0, LED3.anode
  N16: R4.Pin_0, LED4.anode

custom parts:
  HC-SR04: HC-SR04 ultrasound distance sensor
